// Logisim project circuits.circ as structural Verilog: 3 circuits, main circuit MyXOR
module MyXOR (
  input  x,
  input  y,
  output \output 
);

  wire and_1_out, and_2_out, not_1_out, not_2_out;

  not not_1 (not_1_out, x);
  not not_2 (not_2_out, y);
  and and_1 (and_1_out, not_1_out, y);
  and and_2 (and_2_out, x, not_2_out);
  FullAdder fulladder_1 ();  // open: X, Y, CarryIn, sum, CarryOut
  or or_1 (\output , and_1_out, and_2_out);
endmodule

module FullAdder (
  input  X,
  input  Y,
  input  CarryIn,
  output sum,
  output CarryOut
);

  wire not_1_out;

  not not_1 (not_1_out, X);
endmodule

module _4_bit_Ripple_Carry_Adder (
  input  Y3,
  input  Y2,
  input  Y1,
  input  Y0,
  input  X1,
  input  X3,
  input  X2,
  input  X0,
  output Sum4,
  output Sum3,
  output Sum2,
  output Sum1,
  output Sum0
);

  wire fulladder_2_p3, fulladder_2_p5, fulladder_3_p4;

  FullAdder fulladder_1 (.X(Y2), .Y(X2), .CarryIn(fulladder_2_p5));  // open: sum, CarryOut
  // FullAdder fulladder_2: pin names not known; wires that end beside it: Y1, X1, fulladder_2_p3, Sum1, fulladder_2_p5
  // FullAdder fulladder_3: pin names not known; wires that end beside it: Y0, X0, 1'b0, fulladder_3_p4, fulladder_2_p3
endmodule
