// Logisim project fullAdder.circ as structural Verilog: 1 circuit, main circuit main
module main (
  input  A,
  input  B,
  input  carry__in,
  output sum,
  output carry__out
);

  wire and_1_out, and_2_out, xor_1_out;

  xor xor_1 (xor_1_out, A, B);
  and and_1 (and_1_out, A, B);
  xor xor_2 (sum, xor_1_out, carry__in);
  and and_2 (and_2_out, xor_1_out, carry__in);
  or or_1 (carry__out, and_2_out, and_1_out);
endmodule
