// Logisim project halfAdder.circ as structural Verilog: 1 circuit, main circuit main
module main (
  input  A,
  input  B,
  output sum,
  output carry_out
);

  xor xor_1 (sum, A, B);
  and and_1 (carry_out, A, B);
endmodule
