// Logisim project notes3-6-15.circ as structural Verilog: 1 circuit, main circuit main
module main (
  input  x,
  input  y,
  input  A,
  input  B,
  input  A_2,
  input  B_2,
  input  Carry__in,
  output \output ,
  output sum,
  output carry__out,
  output sum_2,
  output carry_out
);

  wire and_1_out, and_2_out, and_3_out, and_5_out, not_1_out, not_2_out, xor_1_out;

  not not_1 (not_1_out, x);
  not not_2 (not_2_out, y);
  xor xor_1 (xor_1_out, A_2, B_2);
  and and_1 (and_1_out, A_2, B_2);
  and and_2 (and_2_out, not_1_out, y);
  and and_3 (and_3_out, x, not_2_out);
  xor xor_2 (sum, A, B);
  and and_4 (carry__out, A, B);
  or or_1 (\output , and_2_out, and_3_out);
  xor xor_3 (sum_2, xor_1_out, Carry__in);
  and and_5 (and_5_out, xor_1_out, Carry__in);
  or or_2 (carry_out, and_5_out, and_1_out);

  // Notes on the sheet:
  //   take in 2 single binary numbers and produce the sum
  //   EXCLUSIVE OR
endmodule
